// Logisim project Control Unit.circ as structural Verilog: 3 circuits, main circuit main
module main (
);

  ALU_Control alu_control_1 ();  // open: Function_Field, ALU_Op, Operation
endmodule

module Control_Unit (
  input  [3:0] Opcode,
  output RegDst,
  output ALUSrc,
  output MemToReg,
  output RegWrite,
  output MemRead,
  output MemWrite,
  output [1:0] ALU_Op
);

  and and_1 (ALU_Op[1], ~Opcode[3], ~Opcode[2], ~Opcode[1], ~Opcode[0]);  // AND_Gate
  and and_2 (MemRead, ~Opcode[3], ~Opcode[2], Opcode[1], Opcode[0]);  // AND_Gate
  and and_3 (MemWrite, Opcode[3], ~Opcode[2], Opcode[1], Opcode[0]);  // AND_Gate
  or or_1 (ALUSrc, MemWrite, MemRead);
  or or_2 (RegWrite, ALU_Op[1], MemRead);

  assign ALU_Op[0] = 1'b0;
  assign MemToReg = MemRead;
  assign RegDst = ALU_Op[1];
endmodule

module ALU_Control (
  input  [3:0] Function_Field,
  input  [1:0] ALU_Op,
  output [2:0] Operation
);

  and and_1 (Operation[2], Function_Field[1], ALU_Op[1]);
  or or_1 (Operation[1], ~Function_Field[2], ~ALU_Op[1]);  // OR_Gate
  and and_2 (Operation[0], Function_Field[0], ALU_Op[1]);
endmodule
