// Logisim project Datapath.circ as structural Verilog: 1 circuit, main circuit main
module main (
  input  PC_Reset,
  input  MemoryToReg,
  input  MemStore,
  input  MemLoad,
  input  RegDestination,
  input  RegWrite,
  input  ALU_Source,
  output ZeroCheck,
  output Overflow
);

  wire Clock_out;
  wire [3:0] multiplexer_1_out;
  wire [15:0] bit_extender_1_out, multiplexer_2_out, multiplexer_3_out, n16_bit_alu_1_result,
       n16_bit_register_file_4_bit_select_1_data_1, n16_bit_register_file_4_bit_select_1_data_2, ram_1_data;
  wire [19:0] adder_1_out, Program_Counter_q, rom_1_data;

  Clock Clock (.out(Clock_out));
  Register #(.width(20)) Program_Counter (
    .D(adder_1_out), .Q(Program_Counter_q), .clk(Clock_out), .clr(PC_Reset));  // open: en
  Adder #(.width(20)) adder_1 (.a(20'h1), .b(Program_Counter_q), .out(adder_1_out));  // open: cin, cout
  ROM #(.addrWidth(20), .dataWidth(20)) rom_1 (.addr(Program_Counter_q), .data(rom_1_data));  // open: sel
  Multiplexer #(.width(4), .enable("false")) multiplexer_1 (
    .in0(rom_1_data[11:8]), .in1(rom_1_data[7:4]), .out(multiplexer_1_out), .sel(RegDestination));
  assign bit_extender_1_out = {{8{rom_1_data[7]}}, rom_1_data[7:0]};  // Bit_Extender bit_extender_1
  _16_bit_Register_File__4_bit_select u_16_bit_register_file_4_bit_select_1 (
    .Data_In(multiplexer_3_out), .Write_Address__rd(multiplexer_1_out),
    .Data_1(n16_bit_register_file_4_bit_select_1_data_1),
    .Data_2(n16_bit_register_file_4_bit_select_1_data_2), .Read_Address_1__rs(rom_1_data[15:12]),
    .RegWrite(RegWrite), .Clock(Clock_out), .Read_Address_2__rt(rom_1_data[11:8]));
  Multiplexer #(.width(16), .enable("false")) multiplexer_2 (
    .in0(n16_bit_register_file_4_bit_select_1_data_2), .in1(bit_extender_1_out), .out(multiplexer_2_out),
    .sel(ALU_Source));
  _16_bit_ALU u_16_bit_alu_1 (
    .Operand_A(n16_bit_register_file_4_bit_select_1_data_1), .Operand_B(multiplexer_2_out),
    .ZeroEquality(ZeroCheck), .Overflow(Overflow), .CarryIn(rom_1_data[18]), .BInvert(rom_1_data[18]),
    .Operation(rom_1_data[17:16]), .Result(n16_bit_alu_1_result));  // open: CarryOut
  RAM #(.addrWidth(16), .dataWidth(16), .bus("separate")) ram_1 (
    .addr(n16_bit_alu_1_result), .din(n16_bit_register_file_4_bit_select_1_data_2), .data(ram_1_data),
    .str(MemStore), .clk(Clock_out), .ld(MemLoad));  // open: sel, clr
  Multiplexer #(.width(16), .enable("false")) multiplexer_3 (
    .in0(n16_bit_alu_1_result), .in1(ram_1_data), .out(multiplexer_3_out), .sel(MemoryToReg));

  // Notes on the sheet:
  //   contents of rom_1 (hex, n*v repeats v):
  //   20702 617f0 14*0 617f0
endmodule
